// Logisim project ampel.circ as structural Verilog: 1 circuit, main circuit main
module main (
);

  wire and_1_out, and_2_out, and_3_out, and_4_out, and_5_out, and_6_out, and_7_out, and_8_out, and_9_out,
       and_10_out, and_11_out, and_12_out, and_13_out, button_1_out, clock_1_out, not_1_out, not_2_out,
       not_3_out, not_4_out, not_5_out, not_6_out, not_7_out, not_8_out, not_9_out, not_10_out, not_11_out,
       not_12_out, not_13_out, not_14_out, not_15_out, not_16_out, not_17_out, not_18_out, not_19_out,
       not_20_out, not_21_out, not_22_out, not_23_out, not_24_out, not_25_out, not_26_out, not_27_out,
       not_28_out, not_29_out, not_30_out, not_31_out, not_32_out, not_33_out, not_34_out, or_1_out,
       or_2_out, or_3_out, or_4_out, or_5_out, s_r_ff_1_q, s_r_ff_2_q, s_r_ff_3_q, s_r_ff_4_q, s_r_ff_5_q,
       s_r_ff_6_q, s_r_ff_7_q, s_r_ff_8_q, s_r_ff_9_q, s_r_ff_10_q, s_r_ff_11_q;
  wire [4:0] counter_2_q;
  wire [8:0] counter_1_q;

  Counter #(.width(9), .max('h1ff)) counter_1 (
    .count(1'b1), .Q(counter_1_q), .clk(clock_1_out));  // open: load, D, carry, clr
  Clock clock_1 (.out(clock_1_out));
  and and_1 (and_1_out, counter_1_q[0], counter_1_q[1], counter_1_q[2], counter_1_q[3], counter_1_q[4], counter_1_q[5], counter_1_q[6], counter_1_q[7], counter_1_q[8]);
  Counter #(.width(5), .max('h1f)) counter_2 (
    .count(and_1_out), .Q(counter_2_q), .clk(clock_1_out), .clr(and_13_out));  // open: load, D, carry
  not not_1 (not_1_out, counter_2_q[0]);
  not not_2 (not_2_out, counter_2_q[1]);
  not not_3 (not_3_out, counter_2_q[2]);
  not not_4 (not_4_out, counter_2_q[3]);
  not not_5 (not_5_out, counter_2_q[4]);
  not not_6 (not_6_out, counter_2_q[2]);
  not not_7 (not_7_out, counter_2_q[3]);
  not not_8 (not_8_out, counter_2_q[4]);
  not not_9 (not_9_out, counter_2_q[0]);
  not not_10 (not_10_out, counter_2_q[3]);
  not not_11 (not_11_out, counter_2_q[4]);
  not not_12 (not_12_out, counter_2_q[1]);
  not not_13 (not_13_out, counter_2_q[2]);
  not not_14 (not_14_out, counter_2_q[4]);
  not not_15 (not_15_out, counter_2_q[0]);
  not not_16 (not_16_out, counter_2_q[1]);
  not not_17 (not_17_out, counter_2_q[2]);
  not not_18 (not_18_out, counter_2_q[3]);
  not not_19 (not_19_out, counter_2_q[4]);
  not not_20 (not_20_out, counter_2_q[0]);
  not not_21 (not_21_out, counter_2_q[2]);
  not not_22 (not_22_out, counter_2_q[3]);
  not not_23 (not_23_out, counter_2_q[1]);
  not not_24 (not_24_out, counter_2_q[3]);
  not not_25 (not_25_out, counter_2_q[3]);
  not not_26 (not_26_out, counter_2_q[0]);
  not not_27 (not_27_out, counter_2_q[1]);
  not not_28 (not_28_out, counter_2_q[2]);
  not not_29 (not_29_out, counter_2_q[3]);
  not not_30 (not_30_out, counter_2_q[4]);
  not not_31 (not_31_out, counter_2_q[3]);
  not not_32 (not_32_out, counter_2_q[2]);
  not not_33 (not_33_out, counter_2_q[3]);
  not not_34 (not_34_out, counter_2_q[4]);
  and and_2 (and_2_out, not_1_out, not_2_out, not_3_out, not_4_out, not_5_out);
  and and_3 (and_3_out, counter_2_q[0], counter_2_q[1], not_6_out, not_7_out, not_8_out);
  and and_4 (and_4_out, not_9_out, counter_2_q[1], counter_2_q[2], not_10_out, not_11_out);
  and and_5 (and_5_out, counter_2_q[0], not_12_out, not_13_out, counter_2_q[3], not_14_out);
  and and_6 (and_6_out, not_15_out, not_16_out, not_17_out, not_18_out, not_19_out);
  and and_7 (and_7_out, not_20_out, counter_2_q[1], not_21_out, not_22_out, counter_2_q[4]);
  and and_8 (and_8_out, counter_2_q[0], not_23_out, counter_2_q[2], not_24_out, counter_2_q[4]);
  and and_9 (and_9_out, counter_2_q[0], counter_2_q[1], counter_2_q[2], not_25_out, counter_2_q[4]);
  and and_10 (and_10_out, not_26_out, not_27_out, not_28_out, not_29_out, not_30_out);
  and and_11 (and_11_out, counter_2_q[0], counter_2_q[1], counter_2_q[2], not_31_out, counter_2_q[4]);
  and and_12 (and_12_out, counter_2_q[0], counter_2_q[1], not_32_out, not_33_out, not_34_out);
  S_R_Flip_Flop s_r_ff_1 (
    .S(and_2_out), .clk(clock_1_out), .R(s_r_ff_2_q), .Q(s_r_ff_1_q));  // open: Qn, preset, reset, en
  S_R_Flip_Flop s_r_ff_2 (
    .S(and_3_out), .clk(clock_1_out), .R(s_r_ff_3_q), .Q(s_r_ff_2_q));  // open: Qn, preset, reset, en
  S_R_Flip_Flop s_r_ff_3 (
    .S(and_4_out), .clk(clock_1_out), .R(s_r_ff_7_q), .Q(s_r_ff_3_q));  // open: Qn, preset, reset, en
  S_R_Flip_Flop s_r_ff_4 (
    .S(and_5_out), .clk(clock_1_out), .R(s_r_ff_6_q), .Q(s_r_ff_4_q));  // open: Qn, preset, reset, en
  S_R_Flip_Flop s_r_ff_5 (
    .S(and_6_out), .clk(clock_1_out), .R(and_5_out), .Q(s_r_ff_5_q));  // open: Qn, preset, reset, en
  S_R_Flip_Flop s_r_ff_6 (
    .S(and_7_out), .clk(clock_1_out), .R(and_5_out), .Q(s_r_ff_6_q));  // open: Qn, preset, reset, en
  S_R_Flip_Flop s_r_ff_7 (
    .S(and_8_out), .clk(clock_1_out), .R(s_r_ff_8_q), .Q(s_r_ff_7_q));  // open: Qn, preset, reset, en
  S_R_Flip_Flop s_r_ff_8 (
    .S(and_9_out), .clk(clock_1_out), .R(s_r_ff_1_q), .Q(s_r_ff_8_q));  // open: Qn, preset, reset, en
  S_R_Flip_Flop s_r_ff_9 (
    .S(and_10_out), .clk(clock_1_out), .R(s_r_ff_11_q), .Q(s_r_ff_9_q));  // open: Qn, preset, reset, en
  S_R_Flip_Flop s_r_ff_10 (
    .S(and_11_out), .clk(clock_1_out), .R(s_r_ff_9_q), .Q(s_r_ff_10_q));  // open: Qn, preset, reset, en
  S_R_Flip_Flop s_r_ff_11 (
    .S(and_12_out), .clk(clock_1_out), .R(s_r_ff_10_q), .Q(s_r_ff_11_q));  // open: Qn, preset, reset, en
  and and_13 (and_13_out, button_1_out, or_2_out);
  or or_1 (or_1_out, s_r_ff_5_q, s_r_ff_6_q);
  or or_2 (or_2_out, s_r_ff_9_q, s_r_ff_10_q);
  or or_3 (or_3_out, s_r_ff_3_q, s_r_ff_7_q);
  or or_4 (or_4_out, s_r_ff_2_q, s_r_ff_7_q);
  or or_5 (or_5_out, s_r_ff_1_q, s_r_ff_8_q);
  LED led_1 (.in(or_3_out));
  LED led_2 (.in(or_4_out));
  LED led_3 (.in(or_5_out));
  LED led_4 (.in(or_1_out));
  LED led_5 (.in(s_r_ff_4_q));
  Button button_1 (.out(button_1_out));

  // Notes on the sheet:
  //   A-Gelb (3)
  //   A-Rot (6)
  //   F-Grün (9)
  //   F-Rot (18)
  //   A-Gelb/Rot (21)
  //   A-Grün (23)
  //   Auto
  //   Fußgänger
endmodule
